# Fritzing sketch spires (saved by Fritzing 1.0.3b)
breadboards: 2

parts:
  Nano = Arduino Nano (Rev3.0)
  RE1 = Rotary Encoder [package=THT]
  S5 = SPST Switch [package=switch-spdt_kit]
  A1 = VL53lox
  U1 = AD9833 Module
  J5 = 3.5mm Audio Jack-wq-pj320b.fzpz [package=audio-jack-3.5mm-smd]  # not connected
  J6 = 3.5mm Audio Jack-wq-pj320b.fzpz [package=audio-jack-3.5mm-smd]  # not connected
  VCC1 = 4 x AAA Battery Mount
  LDR5 = Photocell (LDR) [power=0.25W dark_resistance_@0.01lx=300kΩ light_resistance_@100lx=400Ω luminance=10lx package=THT]  # not connected
  LED8 = LED - 3mm [color="Red (635nm)" current=0.030A package="3 mm [THT]"]  # not connected
  1K = Resistor [tolerance=±5% resistance=1k power=0.25W package=THT]  # not connected
  2_2uF = Electrolytic Capacitor [capacitance=2.2µF voltage=35V package="100 mil [THT, electrolytic]"]  # not connected
  104 = Ceramic Capacitor [capacitance=100nF voltage=16V package="200 mil [THT, multilayer]"]  # not connected
  100uF1 = Electrolytic Capacitor [capacitance=0.1mF voltage=35V package="100 mil [THT, electrolytic]"]  # not connected
  100K = Resistor [tolerance=±5% resistance=100k power=0.25W package=THT]  # not connected
  LM387 = LM386 [package=dip08]
  SPKR1 = Loudspeaker  # not connected
  100u1 = Electrolytic Capacitor [capacitance=0.1mF voltage=35V package="100 mil [THT, electrolytic]"]
  10u1 = Electrolytic Capacitor [capacitance=10µF voltage=35V package="100 mil [THT, electrolytic]"]
  10u2 = Electrolytic Capacitor [capacitance=10µF voltage=35V package="100 mil [THT, electrolytic]"]
  105 = Ceramic Capacitor [capacitance=1µF voltage=16V package="200 mil [THT, multilayer]"]
  104_2 = Ceramic Capacitor [capacitance=100nF voltage=16V package="200 mil [THT, multilayer]"]
  47pf1 = Ceramic Capacitor [capacitance=47pF voltage=16V package="200 mil [THT, multilayer]"]
  104_3 = Ceramic Capacitor [capacitance=100nF voltage=16V package="200 mil [THT, multilayer]"]
  out1 = double row female pin header, 2 pins [form="♀ (female)"]
  out2 = Audio Jack (TRS) 3.5mm [package="PG203J [THT]"]
  10 = Resistor [tolerance=±5% resistance=10 power=0.25W package=THT]
  10K1 = Resistor [tolerance=±5% resistance=10k power=0.25W package=THT]
  10K2 = Rotary Potentiometer (Small) [maximum_resistance=10kΩ knob_status=50% power=0.5W package=THT]
  1-10K1 = Rotary Potentiometer (Small) [maximum_resistance=10kΩ knob_status=50% power=0.5W package=THT]
  AMP1 = double row female pin header, 4 pins [form="♀ (female)"]

nets:
  GND: Nano.GND, A1.Pin_2, U1.DGND
  N1: Nano.D4, RE1.SW-1
  N2: Nano.D5, RE1.Pin-B
  N3: Nano.D6, RE1.Pin-A
  N4: Nano.VIN, S5.S
  V++: Nano.5V
  N5: Nano.A5, A1.Pin_3
  N6: Nano.A4, A1.Pin_4
  N7: Nano.3V3, A1.Pin_1
  N8: RE1.GND, RE1.SW-2, 10u1.-, out1.pin1, out2.Sleeve, 10.Pin_1
  N9: S5.P, VCC1.+
  N10: U1.AGND, VCC1.-
  N11: LM387.GAIN, 10u2.-
  N12: LM387.-IN, LM387.BP, 47pf1.1, 10K1.Pin_0
  N13: LM387.+IN, 1-10K1.wiper
  N14: LM387.V-, 47pf1.0, 104_3.1
  N15: LM387.OUT, 100u1.+, 104_2.0, 104_2.1, 10.Pin_0
  N16: LM387.V+, 104_3.0
  N17: 100u1.-, out1.pin2, out2.Ring
  N18: 10u1.+, 10K1.Pin_1
  N19: 10u2.+, 10K2.leg2
  N20: 105.0, AMP1.pin1, AMP1.pin2
  N21: 105.1, 1-10K1.leg2
  N22: AMP1.pin3, AMP1.pin4

notes:
  blueprint@poetaster.de 2025
  spires v1

custom parts:
  Rotary Encoder: Rotary Encoder with push button
  VL53lox: VL53L0X Time-of-Flight (ToF) Laser Ranging Sensor Breakout.
  AD9833 Module: programmable waveform generator
  3.5mm Audio Jack-wq-pj320b.fzpz: 3.5mm Audio Jack WQP-PJ320B is a SMD jack, dia 1/8 inch, female, right angle and through hole.
  4 x AAA Battery Mount: A 4 x AAA battery pack (4.8 Volts with recharables)
